# Fritzing sketch Circuit Diagram (saved by Fritzing 0.9.3b)

parts:
  Arduino_MEGA_2560 = Arduino Mega 2560 (Rev3)
  Raspberry_Pi2 = Raspberry Pi 2  # not connected
  Bluetooth_Module = Bluetooth HC-06d [package=THT]
  FRONT_Ultrasonic_sensor = hc-sr04  # not connected
  Gyroscope = Tri-Axis Gyro Breakout - L3G4200D  # not connected
  REAR_ultrasonic_sensor = hc-sr04  # not connected
  IR_sensor = Infrared Proximity Sensor  # not connected

nets:
  GND: Arduino_MEGA_2560.GND, Bluetooth_Module.GND
  3V3: Arduino_MEGA_2560.3V3, Bluetooth_Module.VCC
  N1: Arduino_MEGA_2560.D0_RX0, Bluetooth_Module.RXD
  N2: Arduino_MEGA_2560.D1_TX0, Bluetooth_Module.TXD

custom parts:
  Bluetooth HC-06d: Bluetooth HC-06 - face down, pins down 16.5mm x 37.5mm PCB
