# Fritzing sketch Circuit Diagram2 (saved by Fritzing 0.9.3b)
breadboards: 2

parts:
  Arduino_MEGA_2560 = Arduino Mega 2560 (Rev3)
  Raspberry_Pi2 = Raspberry Pi 2  # not connected
  Bluetooth_Module = Bluetooth HC-06d [package=THT]
  REAR_Ultrasonic_sensor = hc-sr04
  Gyroscope = Tri-Axis Gyro Breakout - L3G4200D  # not connected
  FRONT_ultrasonic_sensor = hc-sr04
  IR_sensor = Infrared Proximity Sensor  # not connected

nets:
  N1: Arduino_MEGA_2560.A11, REAR_Ultrasonic_sensor.Trig
  N2: Arduino_MEGA_2560.A12, REAR_Ultrasonic_sensor.Echo
  N3: Arduino_MEGA_2560.A13, FRONT_ultrasonic_sensor.Trig
  N4: Arduino_MEGA_2560.A14, FRONT_ultrasonic_sensor.Echo
  3V3: Arduino_MEGA_2560.3V3, Bluetooth_Module.VCC
  5V: Arduino_MEGA_2560.5V, FRONT_ultrasonic_sensor.VCC
  GND: Arduino_MEGA_2560.GND, Bluetooth_Module.GND, FRONT_ultrasonic_sensor.GND
  N5: Arduino_MEGA_2560.D0_RX0, Bluetooth_Module.RXD
  N6: Arduino_MEGA_2560.D1_TX0, Bluetooth_Module.TXD

custom parts:
  Bluetooth HC-06d: Bluetooth HC-06 - face down, pins down 16.5mm x 37.5mm PCB
