# Fritzing sketch Circuit Diagram (saved by Fritzing 0.9.3b)
breadboards: 2

parts:
  Arduino_MEGA_2560 = Arduino Mega 2560 (Rev3)
  Bluetooth_Module = Bluetooth HC-06d [package=THT]
  REAR_Ultrasonic_sensor = hc-sr04
  FRONT_ultrasonic_sensor = hc-sr04
  LED_(Car_stopped) = LED - 3mm [color="Red (633nm)" package="3 mm [THT]"]
  Part3 = MicroSD Card Module

nets:
  N1: Arduino_MEGA_2560.A8, LED_(Car_stopped).anode
  N2: Arduino_MEGA_2560.A11, REAR_Ultrasonic_sensor.Trig
  N3: Arduino_MEGA_2560.A12, REAR_Ultrasonic_sensor.Echo
  N4: Arduino_MEGA_2560.A13, FRONT_ultrasonic_sensor.Trig
  N5: Arduino_MEGA_2560.A14, FRONT_ultrasonic_sensor.Echo
  GND: Arduino_MEGA_2560.GND, Bluetooth_Module.GND, FRONT_ultrasonic_sensor.GND, Part3.GND
  3V3: Arduino_MEGA_2560.3V3, Bluetooth_Module.VCC
  VCC: Arduino_MEGA_2560.5V, REAR_Ultrasonic_sensor.VCC, FRONT_ultrasonic_sensor.VCC, Part3.VCC
  N6: Arduino_MEGA_2560.D0_RX0, Bluetooth_Module.RXD
  N7: Arduino_MEGA_2560.D1_TX0, Bluetooth_Module.TXD
  N8: Arduino_MEGA_2560.D50, Part3.MISO
  N9: Arduino_MEGA_2560.D51, Part3.MOSI
  N10: Arduino_MEGA_2560.D52, Part3.SCK
  N11: Arduino_MEGA_2560.D53, Part3.CS

custom parts:
  Bluetooth HC-06d: Bluetooth HC-06 - face down, pins down 16.5mm x 37.5mm PCB
