# Fritzing sketch Circuit_Diagram (saved by Fritzing 0.9.3b)
circuit board: 40.9068cm x 16.3522cm

parts:
  Bluetooth_Module = Bluetooth HC-06d [package=THT]
  REAR_Ultrasonic_sensor = hc-sr04
  FRONT_ultrasonic_sensor = hc-sr04
  Micro_SD_card_reader = MicroSD Card Module
  LED_(Backward) = LED - 3mm [color="Red (660nm)" package="3 mm [THT]"]
  LED_(Forward) = LED - 3mm [color="Green (570nm)" package="3 mm [THT]"]
  LED_(Car_Going_Right) = LED - 3mm [color="Blue (470nm)" package="3 mm [THT]"]
  LED_(Car_Turning_Left) = LED - 3mm [color="Blue (470nm)" package="3 mm [THT]"]
  LED_(Car_Warns_of_obstacles) = LED - 3mm [color="Red (660nm)" package="3 mm [THT]"]
  Raspberry_Pi_2 = Raspberry Pi 2  # not connected
  Rear_right_wheel = DC Motor
  Rear_left_wheel = DC Motor
  Front_left_wheel = DC Motor
  Battery_holder = 4 x AAA Battery Mount
  2_1_A_USB_Powerbank = LIPO-2000mAh [package=lipo-2000]
  Front_right_wheel = DC Motor
  Arduino_MEGA_2560 = Arduino Mega 2560 (Rev3)

nets:
  VCC: Bluetooth_Module.VCC, Battery_holder.+, Arduino_MEGA_2560.3V3
  GND: Bluetooth_Module.GND, FRONT_ultrasonic_sensor.GND, Micro_SD_card_reader.GND, Battery_holder.-, Arduino_MEGA_2560.GND
  N1: Bluetooth_Module.TXD, Arduino_MEGA_2560.D1_TX0
  N2: Bluetooth_Module.RXD, Arduino_MEGA_2560.D0_RX0
  VCC_2: REAR_Ultrasonic_sensor.VCC, FRONT_ultrasonic_sensor.VCC, Micro_SD_card_reader.VCC, LED_(Backward).cathode, LED_(Forward).cathode, LED_(Car_Going_Right).cathode, LED_(Car_Turning_Left).cathode, LED_(Car_Warns_of_obstacles).cathode, Arduino_MEGA_2560.5V
  N3: REAR_Ultrasonic_sensor.Trig, REAR_Ultrasonic_sensor.GND, Arduino_MEGA_2560.A11
  N4: REAR_Ultrasonic_sensor.Echo, Arduino_MEGA_2560.A12
  N5: FRONT_ultrasonic_sensor.Trig, Arduino_MEGA_2560.A13
  N6: FRONT_ultrasonic_sensor.Echo, Arduino_MEGA_2560.A14
  N7: Micro_SD_card_reader.MISO, Arduino_MEGA_2560.D50
  N8: Micro_SD_card_reader.MOSI, Arduino_MEGA_2560.D51
  N9: Micro_SD_card_reader.SCK, Arduino_MEGA_2560.D52
  N10: Micro_SD_card_reader.CS, Arduino_MEGA_2560.D53
  N11: LED_(Backward).anode, Arduino_MEGA_2560.A8
  N12: LED_(Forward).anode, Arduino_MEGA_2560.A7
  N13: LED_(Car_Going_Right).anode, Arduino_MEGA_2560.A10
  N14: LED_(Car_Turning_Left).anode, Arduino_MEGA_2560.A5
  N15: LED_(Car_Warns_of_obstacles).anode, Arduino_MEGA_2560.A9
  N16: Rear_right_wheel.pin_1, Rear_left_wheel.pin_1, Front_left_wheel.pin_1, Front_right_wheel.pin_1, Arduino_MEGA_2560.A1
  N17: Rear_right_wheel.pin_2, Front_right_wheel.pin_2, Arduino_MEGA_2560.A0
  N18: Rear_left_wheel.pin_2, Front_left_wheel.pin_2
  N19: 2_1_A_USB_Powerbank.+, 2_1_A_USB_Powerbank.-

notes:
  The RPi is powered by a 2.1 A USB powerbank
  The RPi is connected through a type AB USB cable to the Arduino mega 2560 which has a motor shield mounted on it .

custom parts:
  Bluetooth HC-06d: Bluetooth HC-06 - face down, pins down 16.5mm x 37.5mm PCB
